# Fritzing sketch C_LEDanDigitalemPin (saved by Fritzing 0.9.2b)
circuit board: 8.46667cm x 5.64444cm
breadboards: 1

parts:
  Bauteil1 = Arduino Nano (Rev3.0)
  LED1 = smd LED [color="Green (555nm)" package="0805 [SMD]"]
  R3 = Resistor [tolerance=±5% resistance=220 package=THT]

nets:
  N1: Bauteil1.GND, LED1.cathode
  N2: Bauteil1.D3, R3.Pin_1
  N3: LED1.anode, R3.Pin_0
