# Fritzing sketch 11-motor-betreiben (saved by Fritzing 0.9.3b)
circuit board: 8.46667cm x 5.64444cm
breadboards: 1

parts:
  Bauteil1 = Arduino Nano (Rev3.0)
  VCC1 = 4 x AAA Battery Mount
  M1 = DC Motor
  S1 = H-Bridge with L298N

nets:
  GND: Bauteil1.GND, VCC1.-, S1.GND
  N1: M1.pin_1, S1.M1-02
  N2: M1.pin_2, S1.M1-01
  N3: S1.5V, S1.ENA

custom parts:
  H-Bridge with L298N: h-bridge
