# Fritzing sketch 12-motor-ansteuern (saved by Fritzing 0.9.3b)
circuit board: 8.46667cm x 5.64444cm
breadboards: 1

parts:
  Bauteil1 = Arduino Nano (Rev3.0)
  VCC1 = 4 x AAA Battery Mount
  S1 = H-Bridge with L298N
  M1 = DC Motor

nets:
  GND: Bauteil1.GND, VCC1.-, S1.GND
  N1: Bauteil1.D7, S1.IN2
  N2: Bauteil1.D8, S1.IN1
  N3: Bauteil1.D9, S1.ENA
  N4: S1.M1-01, M1.pin_2
  N5: S1.M1-02, M1.pin_1

custom parts:
  H-Bridge with L298N: h-bridge
