# Fritzing sketch 16-elektrische-leitfaehigkeit-messen (saved by Fritzing 0.9.3b)
circuit board: 8.46667cm x 5.64444cm
breadboards: 1

parts:
  Bauteil1 = Arduino Nano (Rev3.0)
  R1 = Resistor [tolerance=±5% resistance=220 package=THT]
  LED1 = smd LED [color="Green (555nm)" package="0805 [SMD]"]
  LED2 = smd LED [color="Red (633nm)" package="0805 [SMD]"]
  R2 = Resistor [tolerance=±5% resistance=220 package=THT]
  Part3 = FC-28 Soil Hygrometer Module - Probe
  Part4 = FC-28 Soil Hygrometer Module

nets (from the breadboard view):
  N1: Bauteil1.GND, LED1.cathode, LED2.cathode
  N2: Bauteil1.D2, R1.Pin_0
  N3: Bauteil1.D3, R2.Pin_0
  5V: Bauteil1.5V, Part4.VCC
  N4: Bauteil1.A0, Part4.AO
  N5: R1.Pin_1, LED1.anode
  N6: LED2.anode, R2.Pin_1
  N7: Part3.POS, Part4.NEG
  N8: Part3.NEG, Part4.POS

custom parts:
  FC-28 Soil Hygrometer Module - Probe: The FC-28 is a soil hygrometer module that uses the Texas Instruments LM393 comparator chip to provide an analog measurement of soil humidity.
  FC-28 Soil Hygrometer Module: The FC-28 is a soil hygrometer module that uses the Texas Instruments LM393 comparator chip to provide an analog measurement of soil humidity. The digital output is high when soil moisture is over a certain threshold, as determined by adjusting the potentiometer.
